// Logisim project AHEA.circ as structural Verilog: 2 circuits, main circuit main
module main (
  input  G0,
  input  P0,
  input  C0,
  input  G1,
  input  P1,
  input  G2,
  input  P2,
  input  G3,
  input  P3,
  output C1,
  output C2,
  output C3,
  output C4
);

  wire and_1_out, and_2_out, and_3_out, and_4_out, and_5_out, and_6_out, and_7_out, and_8_out, and_9_out,
       and_10_out;

  and and_1 (and_1_out, P0, C0);
  and and_2 (and_2_out, C0, G1);
  and and_3 (and_3_out, C0, P3);
  or or_1 (C1, C0, and_1_out);
  and and_4 (and_4_out, C0, C0);
  and and_5 (and_5_out, C0, C0, C0);
  and and_6 (and_6_out, C0, C0, P0, C0);
  and and_7 (and_7_out, C0, P0, C0);
  and and_8 (and_8_out, C0, C0, P3);
  and and_9 (and_9_out, P3, C0, C0, C0);
  and and_10 (and_10_out, P3, C0, C0, P0, C0);
  or or_2 (C2, G1, and_4_out, and_7_out);
  or or_3 (C3, C0, and_2_out, and_5_out, and_6_out);
  or or_4 (C4, C0, and_3_out, and_8_out, and_9_out, and_10_out);

  assign G0 = C0;
  assign G2 = C0;
  assign G3 = C0;
  assign P1 = C0;
  assign P2 = C0;
endmodule

module AHEAD (
  input  in_1,
  input  [3:0] in_2,
  input  [3:0] in_3,
  output S0,
  output S1,
  output S2,
  output S3
);

  wire and_1_out, and_2_out, and_3_out, and_4_out, main_1_c1, main_1_c2, main_1_c3, xor_1_out, xor_2_out,
       xor_3_out, xor_4_out;

  xor xor_1 (xor_1_out, in_2[0], in_3[0]);
  and and_1 (and_1_out, in_2[0], in_3[0]);
  xor xor_2 (xor_2_out, in_2[1], in_3[1]);
  and and_2 (and_2_out, in_2[1], in_3[1]);
  xor xor_3 (xor_3_out, in_2[2], in_3[2]);
  and and_3 (and_3_out, in_2[2], in_3[2]);
  xor xor_4 (xor_4_out, in_2[3], in_3[3]);
  and and_4 (and_4_out, in_2[3], in_3[3]);
  main main_1 (
    .G0(and_1_out), .P0(xor_1_out), .C0(in_1), .G1(and_2_out), .P1(xor_2_out), .G2(and_3_out),
    .P2(xor_3_out), .G3(and_4_out), .P3(xor_4_out), .C1(main_1_c1), .C2(main_1_c2), .C3(main_1_c3));  // open: C4
  xor xor_5 (S0, in_1, xor_1_out);
  xor xor_6 (S1, xor_2_out, main_1_c1);
  xor xor_7 (S2, xor_3_out, main_1_c2);
  xor xor_8 (S3, xor_4_out, main_1_c3);
endmodule
