// Logisim project USR.circ as structural Verilog: 1 circuit, main circuit main
module main (
  input  I1,
  input  I2,
  input  I0,
  input  D1,
  input  I3,
  input  D0,
  input  [1:0] se,
  input  S,
  input  R,
  output Q0,
  output Q1,
  output Q2,
  output Q3
);

  wire clock_1_out, multiplexer_1_out, multiplexer_2_out, multiplexer_3_out, multiplexer_4_out;

  Clock clock_1 (.out(clock_1_out));
  D_Flip_Flop d_ff_1 (.D(multiplexer_1_out), .clk(clock_1_out), .Q(Q0), .preset(S));  // open: Qn, reset
  Multiplexer #(.select(2)) multiplexer_1 (.in0(D0), .in1(Q1), .in2(I0), .in3(Q0), .out(multiplexer_1_out), .sel(se));
  Multiplexer #(.select(2)) multiplexer_2 (.in0(Q0), .in1(Q2), .in2(I1), .in3(Q1), .out(multiplexer_2_out), .sel(se));
  D_Flip_Flop d_ff_2 (.D(multiplexer_2_out), .clk(clock_1_out), .Q(Q1), .preset(S), .reset(R));  // open: Qn
  Multiplexer #(.select(2)) multiplexer_3 (.in0(Q1), .in1(Q3), .in2(I2), .in3(Q2), .out(multiplexer_3_out), .sel(se));
  D_Flip_Flop d_ff_3 (.D(multiplexer_3_out), .clk(clock_1_out), .Q(Q2), .preset(S), .reset(R));  // open: Qn
  Multiplexer #(.select(2)) multiplexer_4 (.in0(Q2), .in1(D1), .in2(I3), .in3(Q3), .out(multiplexer_4_out), .sel(se));
  D_Flip_Flop d_ff_4 (.D(multiplexer_4_out), .clk(clock_1_out), .Q(Q3), .preset(S), .reset(R));  // open: Qn
endmodule
